# Fritzing sketch cyd esp32 relay lampu (saved by Fritzing 0.9.5d)

parts:
  2_Channel_Relay1 = 2 Channel Power Relay
  LED1 = LEDs [package=led10mm]
  Power_plug1 = Power plug
  A1 = ESP32-2432S028R

nets:
  N1: 2_Channel_Relay1.GND, A1.Pin_5, A1.Pin_9
  N2: 2_Channel_Relay1.IN1, A1.Pin_6
  N3: 2_Channel_Relay1.VCC, A1.Pin_8
  N4: 2_Channel_Relay1.K1-COM, LED1.A
  N5: 2_Channel_Relay1.K1-NO, Power_plug1.VCC
  N6: LED1.C, Power_plug1.GND

notes:
  STEKER PLN
  AC 220V
  Relay Module
  3.3 V
  CYD ESP32 2.8"
  CYD ESP32 - Relay
  3.3V - VCC
  GND - GND
  GPIO22 - IN1

custom parts:
  2 Channel Power Relay: A 2 channel power relay. The module operates at 5V.
  LEDs: LEDs Standard schematic elements and footprints for 5mm, 3mm, 1206, and 0603 sized LEDs. 5mm - Spark Fun Electronics SKU : COM-00529 (and others)
  ESP32-2432S028R: The ESP32-2432S028R development board.
